// Logisim project 8MODC.circ as structural Verilog: 1 circuit, main circuit main
module main (
  output A,
  output B,
  output C
);

  wire Clk_out;

  Clock Clk (.out(Clk_out));
  J_K_Flip_Flop #(.trigger("falling")) j_k_ff_1 (
    .J(1'b1), .clk(Clk_out), .K(1'b1), .Q(A));  // open: Qn, preset, en, reset
  J_K_Flip_Flop #(.trigger("falling")) j_k_ff_2 (.J(1'b1), .clk(A), .K(1'b1), .Q(B));  // open: Qn, preset, en, reset
  J_K_Flip_Flop #(.trigger("falling")) j_k_ff_3 (.J(1'b1), .clk(B), .K(1'b1), .Q(C));  // open: Qn, preset, en, reset
endmodule
