// Logisim project D.circ as structural Verilog: 1 circuit, main circuit main
module main (
  input  D,
  output Q,
  output Q_prime
);

  wire Clk_out, nand_1_out, nand_2_out, not_1_out;

  Clock Clk (.out(Clk_out));
  not not_1 (not_1_out, D);
  nand nand_1 (nand_1_out, D, Clk_out);
  nand nand_2 (nand_2_out, Clk_out, not_1_out);
  nand nand_3 (Q, nand_1_out, Q_prime);
  nand nand_4 (Q_prime, Q, nand_2_out);

  // Notes on the sheet:
  //   D Flip_flop
endmodule
