// Logisim project PIPO.circ as structural Verilog: 1 circuit, main circuit main
module main (
  input  D0,
  input  D1,
  input  D2,
  input  D3,
  output Q0,
  output Q1,
  output Q2,
  output Q3
);

  wire CLK_out;

  Clock CLK (.out(CLK_out));
  D_Flip_Flop FF0 (.clk(CLK_out), .D(D0), .Q(Q0));  // open: Qn, preset, en, reset
  D_Flip_Flop FF1 (.clk(CLK_out), .D(D1), .Q(Q1));  // open: Qn, preset, en, reset
  D_Flip_Flop FF2 (.clk(CLK_out), .D(D2), .Q(Q2));  // open: Qn, preset, en, reset
  D_Flip_Flop FF3 (.clk(CLK_out), .D(D3), .Q(Q3));  // open: Qn, preset, en, reset
endmodule
