// Logisim project PISO.circ as structural Verilog: 1 circuit, main circuit main
module main (
  input  B0,
  input  B1,
  input  B2,
  input  B3,
  input  Shift_Load,
  output Output
);

  wire _1_2_out, _1_out, _2_2_out, _2_out, _3_2_out, _3_out, _4_out, _5_out, _6_out, CLK_out, FF0_q, FF1_q,
       FF2_q, not_1_out;

  not not_1 (not_1_out, Shift_Load);
  Clock CLK (.out(CLK_out));
  and _1 (_1_out, FF0_q, Shift_Load);
  D_Flip_Flop FF0 (.clk(CLK_out), .D(B0), .Q(FF0_q));  // open: Qn, preset, en, reset
  and _2 (_2_out, not_1_out, B1);
  or _1_2 (_1_2_out, _1_out, _2_out);
  and _3 (_3_out, FF1_q, Shift_Load);
  and _4 (_4_out, not_1_out, B2);
  or _2_2 (_2_2_out, _3_out, _4_out);
  D_Flip_Flop FF1 (.clk(CLK_out), .D(_1_2_out), .Q(FF1_q));  // open: Qn, preset, en, reset
  and _5 (_5_out, FF2_q, Shift_Load);
  D_Flip_Flop FF2 (.clk(CLK_out), .D(_2_2_out), .Q(FF2_q));  // open: Qn, preset, en, reset
  and _6 (_6_out, not_1_out, B3);
  or _3_2 (_3_2_out, _5_out, _6_out);
  D_Flip_Flop FF3 (.clk(CLK_out), .D(_3_2_out), .Q(Output));  // open: Qn, preset, en, reset
endmodule
