// Logisim project SIPO.circ as structural Verilog: 1 circuit, main circuit main
module main (
  input  INPUT,
  output Q3,
  output Q2,
  output Q1,
  output Q0
);

  wire CLK_out;

  Clock CLK (.out(CLK_out));
  D_Flip_Flop FF3 (.clk(CLK_out), .D(INPUT), .Q(Q3));  // open: Qn, preset, en, reset
  D_Flip_Flop FF2 (.clk(CLK_out), .D(Q3), .Q(Q2));  // open: Qn, preset, en, reset
  D_Flip_Flop FF1 (.clk(CLK_out), .D(Q2), .Q(Q1));  // open: Qn, preset, en, reset
  D_Flip_Flop FF0 (.clk(CLK_out), .D(Q1), .Q(Q0));  // open: Qn, preset, en, reset
endmodule
