// Logisim project SISO.circ as structural Verilog: 1 circuit, main circuit main
module main (
  input  INPUT,
  output OUTPUT
);

  wire CLK_out, FF1_q, FF2_q, FF3_q;

  Clock CLK (.out(CLK_out));
  D_Flip_Flop FF3 (.clk(CLK_out), .D(INPUT), .Q(FF3_q));  // open: Qn, preset, en, reset
  D_Flip_Flop FF2 (.clk(CLK_out), .D(FF3_q), .Q(FF2_q));  // open: Qn, preset, en, reset
  D_Flip_Flop FF1 (.clk(CLK_out), .D(FF2_q), .Q(FF1_q));  // open: Qn, preset, en, reset
  D_Flip_Flop FF0 (.clk(CLK_out), .D(FF1_q), .Q(OUTPUT));  // open: Qn, preset, en, reset
endmodule
