// Logisim project T.circ as structural Verilog: 1 circuit, main circuit main
module main (
  input  T,
  output Q,
  output Q_prime
);

  wire and_1_out, and_2_out, Clk_out;

  Clock Clk (.out(Clk_out));
  and and_1 (and_1_out, T, Clk_out);
  and and_2 (and_2_out, Clk_out, T);
  nor nor_1 (Q, and_1_out, Q_prime);
  nor nor_2 (Q_prime, Q, and_2_out);

  // Notes on the sheet:
  //   T Flip FLop
endmodule
