// Logisim project full-adder.circ as structural Verilog
module full_adder (
  input  in_1,
  input  in_2,
  input  in_3,
  output out_4,
  output out_5
);

  wire and_1_out, and_2_out, xor_1_out;

  xor xor_1 (xor_1_out, in_3, in_2);
  and and_1 (and_1_out, in_3, in_2);
  and and_2 (and_2_out, in_1, xor_1_out);
  xor xor_2 (out_5, xor_1_out, in_1);
  or or_1 (out_4, and_1_out, and_2_out);
endmodule
