// Logisim project lab.circ as structural Verilog
module NAND___AND (
  input  in_1,
  input  in_2,
  output out_3
);

  wire nand_1_out;

  nand nand_1 (nand_1_out, in_1, in_2);
  nand nand_2 (out_3, nand_1_out, nand_1_out);
endmodule

module NAND___NOT (
  input  in_1,
  output out_2
);

  nand nand_1 (out_2, in_1, in_1);
endmodule

module NAND___OR (
  input  in_1,
  input  in_2,
  output out_3
);

  wire nand_1_out, nand_2_out;

  nand nand_1 (nand_1_out, in_1, in_1);
  nand nand_2 (nand_2_out, in_2, in_2);
  nand nand_3 (out_3, nand_1_out, nand_2_out);
endmodule

module Half___Adder (
  input  X,
  input  y,
  output SUM,
  output CARRY
);

  wire nand_1_out;

  nand nand_1 (nand_1_out, X, y);
  xor xor_1 (CARRY, X, y);
  nand nand_2 (SUM, nand_1_out, nand_1_out);
endmodule

module Full___Adder (
  input  x,
  input  y,
  input  z,
  output SUM,
  output CARRY
);

  wire and_1_out, and_2_out, and_3_out, and_4_out, and_5_out, and_6_out, and_7_out, not_1_out, not_2_out,
       not_3_out;

  not not_1 (not_1_out, x);
  not not_2 (not_2_out, y);
  not not_3 (not_3_out, z);
  and and_1 (and_1_out, not_1_out, not_2_out, z);
  and and_2 (and_2_out, not_1_out, y, not_3_out);
  and and_3 (and_3_out, x, not_2_out, not_3_out);
  and and_4 (and_4_out, x, y, z);
  and and_5 (and_5_out, x, y);
  and and_6 (and_6_out, x, z);
  and and_7 (and_7_out, y, z);
  or or_1 (SUM, and_1_out, and_2_out, and_3_out, and_4_out);
  or or_2 (CARRY, and_5_out, and_6_out, and_7_out);
endmodule

module Full___Adder_2 (
  input  in_1,
  input  in_2,
  input  in_3,
  output sum,
  output carry
);

  wire and_1_out, and_2_out, xor_1_out;

  and and_1 (and_1_out, in_2, in_1);
  xor xor_1 (xor_1_out, in_1, in_2);
  and and_2 (and_2_out, xor_1_out, in_3);
  xor xor_2 (sum, xor_1_out, in_3);
  or or_1 (carry, and_2_out, and_1_out);
endmodule
