// Logisim project lab18sept.circ as structural Verilog: 5 circuits, main circuit main
module main (
  input  A,
  input  B,
  input  C,
  output S,
  output C_2
);

  wire and_1_out, and_2_out, xor_1_out;

  xor xor_1 (xor_1_out, A, B);
  and and_1 (and_1_out, B, A);
  xor xor_2 (S, xor_1_out, C);
  and and_2 (and_2_out, C, xor_1_out);
  or or_1 (C_2, and_2_out, and_1_out);
endmodule

module _8_bit_mux (
  input  i0,
  input  i1,
  input  i2,
  input  i3,
  input  i4,
  input  i5,
  input  i6,
  input  i7,
  input  s2,
  input  s1,
  input  s0,
  output out_12
);

  wire and_1_out, and_2_out, and_3_out, and_4_out, and_5_out, and_6_out, and_7_out, and_8_out, not_1_out,
       not_2_out, not_3_out;

  not not_1 (not_1_out, s2);
  not not_2 (not_2_out, s1);
  not not_3 (not_3_out, s0);
  and and_1 (and_1_out, i0, not_3_out, not_2_out, not_1_out);
  and and_2 (and_2_out, i1, s0, not_2_out, not_1_out);
  and and_3 (and_3_out, i2, not_3_out, s1, not_1_out);
  and and_4 (and_4_out, i3, s0, s1, not_1_out);
  and and_5 (and_5_out, i4, not_3_out, not_2_out, s2);
  and and_6 (and_6_out, i5, s0, not_2_out, s2);
  and and_7 (and_7_out, i6, not_3_out, s1, s2);
  and and_8 (and_8_out, i7, s0, s1, s2);
  or or_1 (out_12, and_1_out, and_2_out, and_3_out, and_4_out, and_5_out, and_6_out, and_7_out, and_8_out);
endmodule

module _8_bit_demux (
  input  s2,
  input  s1,
  input  s0,
  input  enable,
  output d0,
  output d1,
  output d2,
  output d3,
  output d4,
  output d5,
  output d6,
  output d7
);

  wire not_1_out, not_2_out, not_3_out;

  not not_1 (not_1_out, s2);
  not not_2 (not_2_out, s1);
  not not_3 (not_3_out, s0);
  and and_1 (d0, not_3_out, not_2_out, not_1_out, enable);
  and and_2 (d1, s0, not_2_out, not_1_out, enable);
  and and_3 (d2, not_3_out, s1, not_1_out, enable);
  and and_4 (d3, s0, s1, not_1_out, enable);
  and and_5 (d4, not_3_out, not_2_out, s2, enable);
  and and_6 (d5, s0, not_2_out, s2, enable);
  and and_7 (d6, not_3_out, s1, s2, enable);
  and and_8 (d7, s0, s1, s2, enable);
endmodule

module boolean_expression (
  input  [2:0] A_B_C,
  input  ENABLE,
  output out_3
);

  Multiplexer #(.select(3)) multiplexer_1 (
    .in0(1'b0), .in1(1'b0), .in2(1'b1), .in3(1'b1), .in4(1'b1), .in5(1'b1), .in6(1'b1), .in7(1'b1),
    .out(out_3), .sel(A_B_C), .en(ENABLE));

  // Notes on the sheet:
  //   0
  //   1
  //   2
  //   3
  //   4
  //   5
  //   6
  //   7
  //   F = A'(A+B)+(B+AA)(A+C')
endmodule

module adder_substractor (
  output out_1
);

  wire main_1_c_2, main_1_s, main_2_s, main_3_s, undriven, undriven_2, undriven_3, undriven_4, undriven_5,
       undriven_6, undriven_7, undriven_8, xor_1_out, xor_2_out, xor_3_out, xor_4_out;

  xor xor_1 (xor_1_out, undriven, out_1);
  main main_1 (.A(undriven_2), .C(xor_1_out), .S(main_1_s), .C_2(main_1_c_2));  // open: B
  xor xor_2 (xor_2_out, undriven_3, out_1);
  main main_2 (.A(undriven_4), .C(xor_2_out), .S(main_2_s), .C_2(main_1_s));  // open: B
  xor xor_3 (xor_3_out, undriven_5, out_1);
  main main_3 (.A(undriven_6), .C(xor_3_out), .S(main_3_s), .C_2(main_2_s));  // open: B
  xor xor_4 (xor_4_out, undriven_7, out_1);
  main main_4 (.A(undriven_8), .C(xor_4_out), .S(out_1), .C_2(main_3_s));  // open: B
endmodule
