// Logisim project mux.circ as structural Verilog: 1 circuit, main circuit main
module main (
  input  in_1,
  input  in_2,
  input  in_3,
  input  in_4,
  input  in_5,
  input  in_6,
  output \output 
);

  wire and_1_out, and_2_out, and_3_out, and_4_out, not_1_out, not_2_out;

  not not_1 (not_1_out, in_5);
  not not_2 (not_2_out, in_6);
  and and_1 (and_1_out, not_1_out, in_1, not_2_out);
  and and_2 (and_2_out, not_2_out, in_2, in_5);
  and and_3 (and_3_out, in_6, in_3, not_1_out);
  and and_4 (and_4_out, in_5, in_4, in_6);
  or or_1 (\output , and_1_out, and_2_out, and_3_out, and_4_out);

  // Notes on the sheet:
  //   x0
  //   x1
  //   x2
  //   x3
  //   s0
  //   s1
endmodule
