// Logisim project practice.circ as structural Verilog
module decoder (
  input  s2,
  input  s1,
  input  s0,
  input  E,
  output x0,
  output x1,
  output x2,
  output x3,
  output x4,
  output x5,
  output x6,
  output x7
);

  wire not_1_out, not_2_out, not_3_out;

  not not_1 (not_1_out, s2);
  not not_2 (not_2_out, s1);
  not not_3 (not_3_out, s0);
  and and_1 (x0, not_1_out, not_2_out, not_3_out, E);
  and and_2 (x1, not_1_out, not_2_out, s0, E);
  and and_3 (x2, not_1_out, s1, not_3_out, E);
  and and_4 (x3, not_1_out, s1, s0, E);
  and and_5 (x4, s2, not_2_out, not_3_out, E);
  and and_6 (x5, s2, not_2_out, s0, E);
  and and_7 (x6, s2, s1, not_3_out, E);
  and and_8 (x7, s2, s1, s0, E);
endmodule

module decoder_letsc (
  input  s2,
  input  s1,
  input  s0,
  input  E,
  output x0,
  output x1,
  output x2,
  output x3,
  output x4,
  output x5,
  output x6,
  output x7
);

  wire not_1_out, not_2_out, not_3_out, not_4_out, not_5_out, not_6_out, not_7_out, not_8_out, not_9_out,
       not_10_out, not_11_out, not_12_out;

  not not_1 (not_1_out, s2);
  not not_2 (not_2_out, s1);
  not not_3 (not_3_out, s0);
  not not_4 (not_4_out, s2);
  not not_5 (not_5_out, s1);
  not not_6 (not_6_out, s2);
  not not_7 (not_7_out, s0);
  not not_8 (not_8_out, s2);
  not not_9 (not_9_out, s1);
  not not_10 (not_10_out, s0);
  not not_11 (not_11_out, s1);
  not not_12 (not_12_out, s0);
  and and_1 (x7, s2, s1, s0, E);
  and and_2 (x0, not_1_out, not_2_out, not_3_out, E);
  and and_3 (x1, not_4_out, not_5_out, s0, E);
  and and_4 (x2, not_6_out, s1, not_7_out, E);
  and and_5 (x3, not_8_out, s1, s0, E);
  and and_6 (x4, s2, not_9_out, not_10_out, E);
  and and_7 (x5, s2, not_11_out, s0, E);
  and and_8 (x6, s2, s1, not_12_out, E);
endmodule

module encoder (
  input  i0,
  input  i1,
  input  i2,
  input  i3,
  output a1,
  output a0
);

  or or_1 (a1, i2, i3);
  or or_2 (a0, i1, i3);
endmodule
