// Logisim project revision.circ as structural Verilog
module decoder (
  input  enable,
  input  i2,
  input  i2_2,
  input  i2_3,
  output x0,
  output x1,
  output x2,
  output x3,
  output x4,
  output x5,
  output x6,
  output x7
);

  wire not_1_out, not_2_out, not_3_out;

  not not_1 (not_1_out, i2);
  not not_2 (not_2_out, i2_2);
  not not_3 (not_3_out, i2_3);
  and and_1 (x0, not_3_out, not_2_out, not_1_out, enable);
  and and_2 (x1, i2_3, not_2_out, not_1_out, enable);
  and and_3 (x2, not_3_out, i2_2, not_1_out, enable);
  and and_4 (x3, i2_3, i2_2, not_1_out, enable);
  and and_5 (x4, not_3_out, not_2_out, i2, enable);
  and and_6 (x5, i2_3, not_2_out, i2, enable);
  and and_7 (x6, not_3_out, i2_2, i2, enable);
  and and_8 (x7, i2_3, i2_2, i2, enable);
endmodule

module encoder (
  input  i7,
  input  i6,
  input  i5,
  input  i4,
  input  i3,
  input  i2,
  input  i1,
  input  i0,
  output a0,
  output a1,
  output a2
);

  or or_1 (a0, i1, i3, i5, i7);
  or or_2 (a1, i2, i3, i6, i7);
  or or_3 (a2, i4, i5, i6, i7);
endmodule

module multiplexer (
  input  i0,
  input  i1,
  input  i2,
  input  i3,
  input  i4,
  input  i5,
  input  i6,
  input  i7,
  input  s2,
  input  s1,
  input  s0,
  output out
);

  wire and_1_out, and_2_out, and_3_out, and_4_out, and_5_out, and_6_out, and_7_out, and_8_out, not_1_out,
       not_2_out, not_3_out;

  not not_1 (not_1_out, s2);
  not not_2 (not_2_out, s1);
  not not_3 (not_3_out, s0);
  and and_1 (and_1_out, i0, not_3_out, not_2_out, not_1_out);
  and and_2 (and_2_out, i1, s0, not_2_out, not_1_out);
  and and_3 (and_3_out, i2, not_3_out, s1, not_1_out);
  and and_4 (and_4_out, i3, s0, s1, not_1_out);
  and and_5 (and_5_out, i4, not_3_out, not_2_out, s2);
  and and_6 (and_6_out, i5, s0, not_2_out, s2);
  and and_7 (and_7_out, i6, not_3_out, s1, s2);
  and and_8 (and_8_out, i7, s0, s1, s2);
  or or_1 (out, and_1_out, and_2_out, and_3_out, and_4_out, and_5_out, and_6_out, and_7_out, and_8_out);
endmodule

module demultiplexer (
  input  i,
  input  s2,
  input  s1,
  input  s0,
  output o0,
  output o0_2,
  output o0_3,
  output o0_4,
  output o0_5,
  output o0_6,
  output o0_7,
  output o0_8
);

  wire not_1_out, not_2_out, not_3_out;

  not not_1 (not_1_out, s2);
  not not_2 (not_2_out, s1);
  not not_3 (not_3_out, s0);
  and and_1 (o0, i, not_3_out, not_2_out, not_1_out);
  and and_2 (o0_2, i, s0, not_2_out, not_1_out);
  and and_3 (o0_3, i, not_3_out, s1, not_1_out);
  and and_4 (o0_4, i, s0, s1, not_1_out);
  and and_5 (o0_5, i, not_3_out, not_2_out, s2);
  and and_6 (o0_6, i, s0, not_2_out, s2);
  and and_7 (o0_7, i, not_3_out, s1, s2);
  and and_8 (o0_8, i, s0, s1, s2);
endmodule
