// Logisim project sequential_circuit.circ as structural Verilog
module sequential_circuits (
  input  in_1,
  input  in_2,
  output out_3,
  output out_4
);

  nor nor_1 (out_3, in_1, out_4);
  nor nor_2 (out_4, out_3, in_2);
endmodule
